# Fritzing sketch rf_network_arduino (saved by Fritzing 0.9.3b)

parts:
  part = Arduino Uno (Rev3)
  part_2 = NRF24L01+ Breakout Board

nets:
  N1: part.D9_PWM, part_2.CE
  N2: part.D10_PWM/SS, part_2.CS
  N3: part.D11_PWM/MOSI, part_2.MOSI
  N4: part.D12/MISO, part_2.MISO
  N5: part.D13/SCK, part_2.SCK
  3V3: part.3V3, part_2.VCC
  GND: part.GND, part_2.GND
