# Fritzing sketch rf_network_rpiv2 (saved by Fritzing 0.9.3b)

parts:
  part = NRF24L01+ Breakout Board
  part_2 = Raspberry Pi 2

nets:
  GND: part.GND, part_2.GND
  3V3: part.VCC, part_2.3v3, part_2.3V3
  N1: part.CE, part_2.GIPO24
  N2: part.CS, part_2.GIPO25
  N3: part.SCK, part_2.GIPO11
  N4: part.MOSI, part_2.GIPO10
  N5: part.MISO, part_2.GIPO9
